# Fritzing sketch Dice (saved by Fritzing 0.8.5b)
circuit board: 8.46667cm x 5.64444cm
breadboards: 1

parts:
  Part1 = Arduino Uno (Rev3)
  R5 = Resistor [tolerance=±5% resistance=330 package=THT]
  R3 = Resistor [tolerance=±5% resistance=330 package=THT]
  R6 = Resistor [tolerance=±5% resistance=330 package=THT]
  R7 = Resistor [tolerance=±5% resistance=330 package=THT]
  R2 = Resistor [tolerance=±5% resistance=330 package=THT]
  R1 = Resistor [tolerance=±5% resistance=330 package=THT]
  SW_PB = Pushbutton [package="[THT]"]
  R8 = Resistor [tolerance=±5% resistance=10k package=THT]
  R4 = Resistor [tolerance=±5% resistance=330 package=THT]
  ANTNOISE = Antenna
  LED7 = LED - 3mm [color="Red (633nm)" package="3 mm [THT]"]
  LED2 = LED - 3mm [color="Red (633nm)" package="3 mm [THT]"]
  LED1 = LED - 3mm [color="Red (633nm)" package="3 mm [THT]"]
  LED6 = LED - 3mm [color="Red (633nm)" package="3 mm [THT]"]
  LED5 = LED - 3mm [color="Red (633nm)" package="3 mm [THT]"]
  LED4 = LED - 3mm [color="Red (633nm)" package="3 mm [THT]"]
  LED3 = LED - 3mm [color="Red (633nm)" package="3 mm [THT]"]

nets:
  N1: Part1.A0, ANTNOISE.antenna_lead
  N2: Part1.D9_PWM, LED3.anode
  N3: Part1.D10_PWM/SS, LED2.anode
  N4: Part1.D11_PWM/MOSI, LED1.anode
  GND: Part1.D2, Part1.GND, R5.Pin_1, R3.Pin_1, R6.Pin_1, R7.Pin_1, R2.Pin_1, R1.Pin_1, SW_PB.Pin_1, SW_PB.Pin_2, SW_PB.Pin_3, SW_PB.Pin_4, R8.Pin_1, R4.Pin_1
  N5: Part1.D3_PWM, LED7.anode
  N6: Part1.D4, LED6.anode
  N7: Part1.D5_PWM, LED5.anode
  N8: Part1.D6_PWM, LED4.anode
  5V: Part1.5V, R8.Pin_0
  N9: R5.Pin_0, LED5.cathode
  N10: R3.Pin_0, LED3.cathode
  N11: R6.Pin_0, LED6.cathode
  N12: R7.Pin_0, LED7.cathode
  N13: R2.Pin_0, LED2.cathode
  N14: R1.Pin_0, LED1.cathode
  N15: R4.Pin_0, LED4.cathode
